# Fritzing sketch vmac (saved by Fritzing 1.0.2b)
circuit board: 8.46667cm x 5.64444cm

parts:
  WeMos_D1_Mini1 = WeMos D1 Mini
  Part1 = Adafruit OLED Monochrome 1.3in 128x64 with STEMMA QT [part_number="Adafruit #938"]
  J1 = Basic Servo
  LED2 = LED - 5mm [color="Red (633nm)" current=0.030A package="5 mm [THT]"]
  LED3 = LED - 5mm [color="Red (633nm)" current=0.030A package="5 mm [THT]"]
  LED4 = LED - 5mm [color="Red (633nm)" current=0.030A package="5 mm [THT]"]
  LED5 = LED - 5mm [color="Red (633nm)" current=0.030A package="5 mm [THT]"]
  LED6 = LED - 5mm [color="Red (633nm)" current=0.030A package="5 mm [THT]"]
  LED1 = LED - 5mm [color="Red (633nm)" current=0.030A package="5 mm [THT]"]
  LED7 = LED - 5mm [color="Red (633nm)" current=0.030A package="5 mm [THT]"]
  LED8 = LED - 5mm [color="Red (633nm)" current=0.030A package="5 mm [THT]"]
  R2 = Resistor [tolerance=±5% power=0.25W resistance=10k package=THT]
  Part3 = RFID-RC522 [part_number=101218]
  S1 = SWITCH-MOMENTARY-2 [package=tactile-pth-12mm]
  JACK1 = 2.1mm Barrel Jack with Terminal Block
  Part2 = Adafruit PCA9685 PWM/Servo Breakout [part_number=815]

nets (from the breadboard view):
  3V3: WeMos_D1_Mini1.3V3, R2.Pin_0, Part3.3.3V
  VCC: WeMos_D1_Mini1.5V, Part1.VCC, Part2.VCC
  N1: WeMos_D1_Mini1.D0, R2.Pin_1, S1.1
  N2: WeMos_D1_Mini1.D1, Part1.SCL, Part2.SCL
  N3: WeMos_D1_Mini1.D2, Part1.SDA, Part2.SDA
  N4: WeMos_D1_Mini1.D5, Part3.SCK
  N5: WeMos_D1_Mini1.D6, Part3.MOSI
  N6: WeMos_D1_Mini1.D7, Part3.MISO
  N7: WeMos_D1_Mini1.D8, Part3.SDA
  GND: Part1.GND, JACK1.NEG, Part2.GND
  N8: J1.gnd, S1.2
  N9: J1.vcc, Part2.5.0V
  N10: J1.pulse, Part2.PWM0
  N11: LED2.anode, Part2.PWM11
  N12: LED3.cathode, LED4.cathode
  N13: LED3.anode, Part2.PWM10
  N14: LED4.anode, Part2.PWM9
  N15: LED5.cathode, LED6.cathode
  N16: LED5.anode, Part2.PWM8
  N17: LED6.anode, Part2.PWM7
  N18: LED1.anode, Part2.PWM4
  N19: LED7.cathode, LED8.cathode
  N20: LED7.anode, Part2.PWM6
  N21: LED8.anode, Part2.PWM5
  N22: JACK1.POS, Part2.PWRIN

custom parts:
  Adafruit OLED Monochrome 1.3in 128x64 with STEMMA QT: These displays are small, only about 1.3" diagonal, but very readable due to the high contrast of an OLED display. This display is made of 128x64 individual white OLED pixels, each one is turned on or off by the controller chip. Because the display makes its own light, no backlight is required. This reduces the power required to run the OLED and is why the display has such high contrast; we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
  Adafruit PCA9685 PWM/Servo Breakout: Using only two pins, control 16 free-running PWM outputs! I2C-controlled PWM driver with a built in clock. Unlike the TLC5940 family, you do not need to continuously send it signal tying up your microcontroller, its completely free running! 5V compliant, which means you can control it from a 3.3V microcontroller and still safely drive up to 6V outputs (this is good for when you want to control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
